// Logisim project ex4.circ as structural Verilog: 1 circuit, main circuit Split
module Split (
  input  [7:0] In1,
  output Out1,
  output [7:0] Out2
);

  wire [5:0] not_2_out;
  wire [7:0] not_1_out;

  not not_1 (not_1_out[0], In1[0]);
  not not_2 (not_2_out[0], In1[1]);
  not not_3 (not_2_out[1], In1[2]);
  not not_4 (not_2_out[2], In1[3]);
  not not_5 (not_2_out[3], In1[4]);
  not not_6 (not_2_out[4], In1[5]);
  not not_7 (not_2_out[5], In1[6]);
  not not_8 (not_1_out[7], In1[7]);
  and and_1 (Out1, In1[0], In1[7]);
  Adder adder_1 (.a({not_1_out[7], not_2_out, not_1_out[0]}), .b(8'h1), .out(Out2));  // open: cin, cout

  // Notes on the sheet:
  //   PUT CIRCUITRY HERE
endmodule
